// Logisim project B2_Group6.circ as structural Verilog: 1 circuit, main circuit main
module main (
  input  S2,
  input  S1,
  input  S0,
  input  A3,
  input  A2,
  input  A1,
  input  A0,
  input  B3,
  input  B2,
  input  B1,
  input  B0,
  output Y3,
  output Y2,
  output Y1,
  output Y0,
  output SF,
  output CF,
  output OF,
  output ZF
);

  wire n7402_1__13__4y, n7404_1__2__1y, n7404_1__4__2y, n7404_1__6__3y, n7404_1__8__4y, n7404_1__10__5y,
       n7404_1__12__6y, n7404_2__2__1y, n7404_2__4__2y, n7404_2__6__3y, n7404_2__8__4y, n7404_2__10__5y,
       n7404_2__12__6y, n7408_1__3__1y, n7408_1__6__2y, n7408_1__8__3y, n7408_1__11__4y, n7432_1__3__1y,
       n7432_1__6__2y, n7432_1__8__3y, n7432_1__11__4y, n7432_2__3__1y, n7432_2__6__2y, n7432_2__8__3y,
       n7432_2__11__4y, n7483_1__2__s3, n7483_1__6__s2, n7483_1__9__s1, n7483_1__14__cout, n7483_1__15__s4,
       n7486_1__3__1y, n7486_1__6__2y, n7486_1__8__3y, n7486_1__11__4y, n74157_1__4__y1, n74157_1__7__y2,
       n74157_1__9__y3, n74157_1__12__y4, n74157_2__4__y1, n74157_2__7__y2, n74157_2__9__y3,
       n74157_2__12__y4, n74157_4__4__y1, n74157_4__7__y2, n74157_4__9__y3, n74157_4__12__y4,
       n74157_5__4__y1, n74157_5__7__y2, n74157_5__9__y3, n74157_5__12__y4;

  _7408 u_7408_1 (
    ._1__1A(A0), ._2__1B(B0), ._3__1Y(n7408_1__3__1y), ._4__2A(A1), ._5__2B(B1), ._6__2Y(n7408_1__6__2y),
    ._7__GND(1'b0), ._14__Vcc(1'b1), ._13__4B(A3), ._12__4A(B3), ._11__4Y(n7408_1__11__4y), ._10__3B(A2),
    ._9__3A(B2), ._8__3Y(n7408_1__8__3y));
  _74157 u_74157_1 (
    ._1__S(S1), ._2__A1(n7432_1__3__1y), ._3__B1(n7408_1__3__1y), ._4__Y1(n74157_1__4__y1),
    ._5__A2(n7432_1__6__2y), ._6__B2(n7408_1__6__2y), ._7__Y2(n74157_1__7__y2), ._8__GND(1'b0),
    ._16__Vcc(1'b1), ._15__G(1'b0), ._14__A4(n7432_1__8__3y), ._13__B4(n7408_1__8__3y),
    ._12__Y4(n74157_1__12__y4), ._11__A3(n7432_1__11__4y), ._10__B3(n7408_1__11__4y), ._9__Y3(n74157_1__9__y3));
  _7404 u_7404_1 (
    ._1__1A(A0), ._2__1Y(n7404_1__2__1y), ._3__2A(n7483_1__14__cout), ._4__2Y(n7404_1__4__2y), ._5__3A(A3),
    ._6__3Y(n7404_1__6__3y), ._7__GND(1'b0), ._14__Vcc(1'b1), ._13__6A(A1), ._12__6Y(n7404_1__12__6y),
    ._11__5A(n7432_2__11__4y), ._10__5Y(n7404_1__10__5y), ._9__4A(A2), ._8__4Y(n7404_1__8__4y));
  _7432 u_7432_1 (
    ._1__1A(B0), ._2__1B(A0), ._3__1Y(n7432_1__3__1y), ._4__2A(B1), ._5__2B(A1), ._6__2Y(n7432_1__6__2y),
    ._7__GND(1'b0), ._14__Vcc(1'b1), ._13__4B(B3), ._12__4A(A3), ._11__4Y(n7432_1__11__4y), ._10__3B(B2),
    ._9__3A(A2), ._8__3Y(n7432_1__8__3y));
  _74157 u_74157_2 (
    ._1__S(n7432_2__6__2y), ._2__A1(n7404_1__2__1y), ._3__B1(A0), ._4__Y1(n74157_2__4__y1),
    ._5__A2(n7404_1__12__6y), ._6__B2(A1), ._7__Y2(n74157_2__7__y2), ._8__GND(1'b0), ._16__Vcc(1'b1),
    ._15__G(1'b0), ._14__A4(n7404_1__6__3y), ._13__B4(A3), ._12__Y4(n74157_2__12__y4),
    ._11__A3(n7404_1__8__4y), ._10__B3(A2), ._9__Y3(n74157_2__9__y3));
  _74157 u_74157_3 (
    ._1__S(n7432_2__11__4y), ._2__A1(n74157_1__4__y1), ._3__B1(n7483_1__9__s1), ._4__Y1(Y0),
    ._5__A2(n74157_1__9__y3), ._6__B2(n7483_1__15__s4), ._7__Y2(SF), ._8__GND(1'b0), ._16__Vcc(1'b1),
    ._15__G(1'b0), ._14__A4(n74157_1__7__y2), ._13__B4(n7483_1__6__s2), ._12__Y4(Y1),
    ._11__A3(n74157_1__12__y4), ._10__B3(n7483_1__2__s3), ._9__Y3(Y2));
  _7404 u_7404_2 (
    ._1__1A(B0), ._2__1Y(n7404_2__2__1y), ._3__2A(S1), ._4__2Y(n7404_2__4__2y), ._5__3A(B3),
    ._6__3Y(n7404_2__6__3y), ._7__GND(1'b0), ._14__Vcc(1'b1), ._13__6A(B1), ._12__6Y(n7404_2__12__6y),
    ._11__5A(S0), ._10__5Y(n7404_2__10__5y), ._9__4A(B2), ._8__4Y(n7404_2__8__4y));
  _7402 u_7402_1 (
    ._1__1Y(ZF), ._2__1A(n7432_2__8__3y), ._3__1B(n7432_2__3__1y), ._4__2Y(CF), ._5__2A(n7404_1__4__2y),
    ._6__2B(n7404_1__10__5y), ._7__GND(1'b0), ._14__Vcc(1'b1), ._13__4Y(n7402_1__13__4y),
    ._12__4B(n7486_1__8__3y), ._11__4A(n7486_1__8__3y), ._10__3Y(OF), ._9__3B(n7402_1__13__4y),
    ._8__3A(n7404_1__10__5y));
  _74157 u_74157_4 (
    ._1__S(S1), ._2__A1(n7404_2__2__1y), ._3__B1(B0), ._4__Y1(n74157_4__4__y1), ._5__A2(n7404_2__12__6y),
    ._6__B2(B1), ._7__Y2(n74157_4__7__y2), ._8__GND(1'b0), ._16__Vcc(1'b1), ._15__G(1'b0),
    ._14__A4(n7404_2__6__3y), ._13__B4(B3), ._12__Y4(n74157_4__12__y4), ._11__A3(n7404_2__8__4y),
    ._10__B3(B2), ._9__Y3(n74157_4__9__y3));
  _7483 u_7483_1 (
    ._1__A4(n74157_5__7__y2), ._2__S3(n7483_1__2__s3), ._3__A3(n74157_2__9__y3), ._4__B3(n74157_5__9__y3),
    ._5__Vcc(1'b1), ._6__S2(n7483_1__6__s2), ._7__B2(n74157_2__7__y2), ._8__A2(n74157_5__12__y4),
    ._16__B4(n74157_2__12__y4), ._15__S4(n7483_1__15__s4), ._14__Cout(n7483_1__14__cout),
    ._13__Cin(n7404_2__10__5y), ._12__GND(1'b0), ._11__B1(n74157_2__4__y1), ._10__A1(n74157_5__4__y1),
    ._9__S1(n7483_1__9__s1));
  _7432 u_7432_2 (
    ._1__1A(Y2), ._2__1B(SF), ._3__1Y(n7432_2__3__1y), ._4__2A(S0), ._5__2B(n7404_2__4__2y),
    ._6__2Y(n7432_2__6__2y), ._7__GND(1'b0), ._14__Vcc(1'b1), ._13__4B(S2), ._12__4A(n7404_2__10__5y),
    ._11__4Y(n7432_2__11__4y), ._10__3B(Y0), ._9__3A(Y1), ._8__3Y(n7432_2__8__3y));
  _74157 u_74157_5 (
    ._1__S(n7486_1__3__1y), ._2__A1(n74157_4__4__y1), ._3__B1(1'b0), ._4__Y1(n74157_5__4__y1),
    ._5__A2(n74157_4__12__y4), ._6__B2(1'b0), ._7__Y2(n74157_5__7__y2), ._8__GND(1'b0), ._16__Vcc(1'b1),
    ._15__G(1'b0), ._14__A4(n74157_4__7__y2), ._13__B4(1'b0), ._12__Y4(n74157_5__12__y4),
    ._11__A3(n74157_4__9__y3), ._10__B3(1'b0), ._9__Y3(n74157_5__9__y3));
  _7486 u_7486_1 (
    ._1__1A(S0), ._2__1B(S1), ._3__1Y(n7486_1__3__1y), ._4__2A(n74157_2__12__y4), ._5__2B(n74157_5__7__y2),
    ._6__2Y(n7486_1__6__2y), ._7__GND(1'b0), ._14__Vcc(1'b1), ._13__4B(n7483_1__15__s4),
    ._12__4A(n7483_1__14__cout), ._11__4Y(n7486_1__11__4y), ._10__3B(n7486_1__11__4y),
    ._9__3A(n7486_1__6__2y), ._8__3Y(n7486_1__8__3y));

  assign Y3 = SF;
endmodule
