// Logisim project B2_Group6.circ as structural Verilog: 6 circuits, main circuit main
module main (
  input  [31:0] A,
  input  [31:0] B,
  output out_3,
  output [4:0] out_4,
  output [4:0] out_5,
  output [11:0] out_6,
  output [31:0] out_7,
  output [31:0] out_8,
  output [31:0] OUTPUT
);

  wire EXPONENT_COMPARATOR_selector, not_1_out;
  wire [11:0] _1ST_NORMAL_e_out, EXPONENT_COMPARATOR_diff_e;
  wire [30:0] adder_1_out;
  wire [31:0] _1ST_NORMAL_s__out, _2ND_NORMAL_s__out, multiplexer_1_out, multiplexer_3_out,
       n2_s_complement_1_out, n2_s_complement_2_out, negator_1_out, ROUNDING_out;

  Comparator___Bit_Extender EXPONENT_COMPARATOR (
    .B(B[30:19]), .A(A[30:19]), .SELECTOR(EXPONENT_COMPARATOR_selector), .DIFF_E(EXPONENT_COMPARATOR_diff_e),
    .LARGER_E(out_6));
  Shifting_Logic SHIFTING_AMOUNT_CALC (.E__IN(EXPONENT_COMPARATOR_diff_e), .SHIFT_AMT(out_5));
  _2_s_Complement u_2_s_complement_1 (.IN(A[18:0]), .SIGN(A[31]), .OUT(n2_s_complement_1_out));
  not not_1 (not_1_out, EXPONENT_COMPARATOR_selector);
  Multiplexer #(.width(32), .enable("false")) multiplexer_1 (
    .in0(n2_s_complement_1_out), .in1(n2_s_complement_2_out), .out(multiplexer_1_out),
    .sel(EXPONENT_COMPARATOR_selector));
  Shifter #(.width(32), .shift("ar")) shifter_1 (.in(multiplexer_1_out), .\dist (out_5), .out(out_7));
  Multiplexer #(.width(32), .enable("false")) multiplexer_2 (
    .in0(n2_s_complement_1_out), .in1(n2_s_complement_2_out), .out(out_8), .sel(not_1_out));
  Adder #(.width(32)) adder_1 (.a(out_8), .b(out_7), .out({out_3, adder_1_out}), .cin(1'b0));  // open: cout
  Multiplexer #(.width(32), .enable("false")) multiplexer_3 (
    .in0({out_3, adder_1_out}), .in1(negator_1_out), .out(multiplexer_3_out), .sel(out_3));
  _2_s_Complement u_2_s_complement_2 (.IN(B[18:0]), .SIGN(B[31]), .OUT(n2_s_complement_2_out));
  Negator #(.width(32)) negator_1 (.in({out_3, adder_1_out}), .out(negator_1_out));
  Normalize _1ST_NORMAL (
    .S__IN(multiplexer_3_out), .E__IN(out_6), .BITS_N(out_4), .S__OUT(_1ST_NORMAL_s__out),
    .E_OUT(_1ST_NORMAL_e_out));
  Normalize _2ND_NORMAL (
    .S__IN(ROUNDING_out), .E__IN(_1ST_NORMAL_e_out),
    .S__OUT({_2ND_NORMAL_s__out[31:29], OUTPUT[18:0], _2ND_NORMAL_s__out[9:0]}), .E_OUT(OUTPUT[30:19]));  // open: BITS_N
  Rounding ROUNDING (.IN(_1ST_NORMAL_s__out), .OUT(ROUNDING_out));

  assign OUTPUT[31] = out_3;

  // Notes on the sheet:
  //   ADDER
endmodule

module Comparator___Bit_Extender (
  input  [11:0] B,
  input  [11:0] A,
  output SELECTOR,
  output [11:0] DIFF_E,
  output [11:0] LARGER_E
);

  wire comparator_1_eq, comparator_1_gt, comparator_1_lt;
  wire [11:0] multiplexer_1_out;

  Comparator #(.width(12), .mode("unsigned")) comparator_1 (
    .a(A), .b(B), .gt(comparator_1_gt), .eq(comparator_1_eq), .lt(comparator_1_lt));
  or or_1 (SELECTOR, comparator_1_gt, comparator_1_eq);
  Multiplexer #(.width(12), .enable("false")) multiplexer_1 (.in0(A), .in1(B), .out(multiplexer_1_out), .sel(SELECTOR));
  Multiplexer #(.width(12), .enable("false")) multiplexer_2 (.in0(A), .in1(B), .out(LARGER_E), .sel(comparator_1_lt));
  Subtractor #(.width(12)) subtractor_1 (.a(LARGER_E), .b(multiplexer_1_out), .out(DIFF_E));  // open: bin, bout
endmodule

// 2'S COMPL.
module _2_s_Complement (
  input  [18:0] IN,
  input  SIGN,
  output [31:0] OUT
);

  wire [31:0] negator_1_out;

  Negator #(.width(32)) negator_1 (.in({3'b001, IN, {10{1'b0}}}), .out(negator_1_out));
  Multiplexer #(.width(32), .enable("false")) multiplexer_1 (
    .in0({3'b001, IN, {10{1'b0}}}), .in1(negator_1_out), .out(OUT), .sel(SIGN));
endmodule

module Shifting_Logic (
  input  [11:0] E__IN,
  output [4:0] SHIFT_AMT
);

  wire comparator_1_gt;
  wire [11:5] multiplexer_1_out;

  Comparator #(.width(12), .mode("unsigned")) comparator_1 (
    .a(12'h15), .b(E__IN), .gt(comparator_1_gt));  // open: eq, lt
  Multiplexer #(.width(12), .enable("false")) multiplexer_1 (
    .in0(12'h15), .in1(E__IN), .out({multiplexer_1_out, SHIFT_AMT}), .sel(comparator_1_gt));
endmodule

module Normalize (
  input  [31:0] S__IN,
  input  [11:0] E__IN,
  output [4:0] BITS_N,
  output [31:0] S__OUT,
  output [11:0] E_OUT
);

  wire comparator_1_lt;
  wire [4:0] bitfinder_1_index, subtractor_2_out, subtractor_3_out;
  wire [11:0] adder_1_out, bit_extender_1_out, bit_extender_2_out, subtractor_4_out;
  wire [31:0] shifter_1_out, shifter_2_out;

  BitFinder #(.width(32), .\type ("high1")) bitfinder_1 (.in(S__IN), .index(bitfinder_1_index));  // open: found
  Subtractor #(.width(5)) subtractor_1 (.a({5{1'b1}}), .b(bitfinder_1_index), .out(BITS_N));  // open: bin, bout
  Comparator #(.width(5)) comparator_1 (.a(5'b00010), .b(BITS_N), .lt(comparator_1_lt));  // open: gt, eq
  Subtractor #(.width(5)) subtractor_2 (.a(5'b00010), .b(BITS_N), .out(subtractor_2_out));  // open: bin, bout
  Subtractor #(.width(5)) subtractor_3 (.a(BITS_N), .b(5'b00010), .out(subtractor_3_out));  // open: bin, bout
  assign bit_extender_1_out = {{7{1'b0}}, subtractor_2_out};  // Bit_Extender bit_extender_1
  assign bit_extender_2_out = {{7{1'b0}}, subtractor_3_out};  // Bit_Extender bit_extender_2
  Shifter #(.width(32), .shift("lr")) shifter_1 (.in(S__IN), .\dist (subtractor_2_out), .out(shifter_1_out));
  Shifter #(.width(32)) shifter_2 (.in(S__IN), .\dist (subtractor_3_out), .out(shifter_2_out));
  Adder #(.width(12)) adder_1 (.a(bit_extender_1_out), .b(E__IN), .out(adder_1_out));  // open: cin, cout
  Subtractor #(.width(12)) subtractor_4 (.a(E__IN), .b(bit_extender_2_out), .out(subtractor_4_out));  // open: bin, bout
  Multiplexer #(.width(32), .enable("false")) multiplexer_1 (
    .in0(shifter_1_out), .in1(shifter_2_out), .out(S__OUT), .sel(comparator_1_lt));
  Multiplexer #(.width(12), .enable("false")) multiplexer_2 (
    .in0(adder_1_out), .in1(subtractor_4_out), .out(E_OUT), .sel(comparator_1_lt));
endmodule

// 1
module Rounding (
  input  [31:0] IN,
  output [31:0] OUT
);

  wire and_1_out, not_1_out, not_2_out;
  wire [1:0] not_3_out;
  wire [21:0] adder_1_out;

  not not_1 (not_1_out, IN[8]);
  not not_2 (not_2_out, IN[7]);
  and and_1 (and_1_out, IN[9], not_1_out, not_2_out);
  Adder #(.width(22)) adder_1 (.a({22{1'b0}}), .b(IN[31:10]), .out(adder_1_out), .cin(1'b1));  // open: cout
  not not_3 (not_3_out[0], IN[9]);
  or or_1 (not_3_out[1], not_3_out[0], and_1_out);
  Multiplexer #(.select(2), .width(22), .enable("false")) multiplexer_1 (
    .in0(adder_1_out), .in2({IN[31:11], 1'b0}), .in3(IN[31:10]), .out(OUT[31:10]), .sel(not_3_out));  // open: in1

  assign OUT[9:0] = {10{1'b0}};
endmodule
