// Logisim project 4_bit_PC.circ as structural Verilog: 8 circuits, main circuit Data Memory
module Data_Memory (
  input  Mem_write,
  input  Mem_read,
  input  [3:0] Address,
  input  [3:0] Write_Data,
  input  Clock,
  input  Reset,
  output [3:0] Read_Data
);

  wire not_1_out;

  not not_1 (not_1_out, Clock);
  RAM #(.addrWidth(4), .dataWidth(4), .bus("separate")) ram_1 (
    .addr(Address), .din(Write_Data), .data(Read_Data), .str(Mem_write), .clk(not_1_out), .ld(Mem_read),
    .clr(Reset));  // open: sel
endmodule

module Instruction (
  input  [7:0] PC,
  output [3:0] Opcode,
  output [3:0] Instruction_8_11,
  output [3:0] Instruction_4_7,
  output [3:0] Instruction_0_3
);

  ROM #(.dataWidth(16)) rom_1 (
    .addr(PC), .data({Opcode, Instruction_8_11, Instruction_4_7, Instruction_0_3}), .sel(1'b1));

  // Notes on the sheet:
  //   contents of rom_1 (hex, n*v repeats v):
  //   8023 8025 120 1120 2120 5120 d120 8023 b102 f102 4102 6102 7103 3310 e320 3320 c000
endmodule

// Pc
module PC (
  input  [7:0] PC_in,
  input  Clock,
  input  Reset,
  output [7:0] PC_out
);

  Register PC (.D(PC_in), .Q(PC_out), .clk(Clock), .clr(Reset));  // open: en
endmodule

module ALU (
  input  [2:0] ALU_op,
  input  [3:0] A,
  input  [3:0] B,
  output [3:0] Result,
  output Zero
);

  wire [3:0] adder_1_out, and_1_out, nor_1_out, or_1_out, shifter_1_out, shifter_2_out, subtractor_1_out;

  assign or_1_out = A | B;  // OR_Gate or_1, 4 bits wide
  assign nor_1_out = ~(A | B);  // NOR_Gate nor_1, 4 bits wide
  assign and_1_out = A & B;  // AND_Gate and_1, 4 bits wide
  Adder #(.width(4)) adder_1 (.a(A), .b(B), .out(adder_1_out), .cin(1'b0));  // open: cout
  Subtractor #(.width(4)) subtractor_1 (.a(A), .b(B), .out(subtractor_1_out), .bin(1'b0));  // open: bout
  Shifter #(.width(4), .shift("lr")) shifter_1 (.in(A), .\dist (B[1:0]), .out(shifter_1_out));
  Shifter #(.width(4)) shifter_2 (.in(A), .\dist (B[1:0]), .out(shifter_2_out));
  Multiplexer #(.select(3), .width(4), .enable("false")) multiplexer_1 (
    .in0(or_1_out), .in1(nor_1_out), .in2(and_1_out), .in3(adder_1_out), .in4(subtractor_1_out),
    .in5(shifter_1_out), .in6(4'b0000), .in7(shifter_2_out), .out(Result), .sel(ALU_op));
  nor nor_2 (Zero, Result[0], Result[1], Result[2], Result[3]);

  // Notes on the sheet:
  //   See shift amount 
endmodule

module Control (
  input  [3:0] opcode,
  output RegDST,
  output Jump,
  output Branch,
  output Branch_NE,
  output MemRead,
  output MemToReg,
  output MemWrite,
  output ALUSrc,
  output RegWrite,
  output [2:0] ALUOp,
  output [11:0] out_12
);

  ROM #(.addrWidth(4), .dataWidth(12)) rom_1 (
    .addr(opcode),
    .data({out_12[11], Jump, Branch, Branch_NE, MemRead, MemToReg, MemWrite, ALUSrc, out_12[3], ALUOp}),
    .sel(1'b1));

  assign {out_12[10:4], out_12[2:0]} = {Jump, Branch, Branch_NE, MemRead, MemToReg, MemWrite, ALUSrc, ALUOp};
  assign RegDST = out_12[11];
  assign RegWrite = out_12[3];

  // Notes on the sheet:
  //   contents of rom_1 (hex, n*v repeats v):
  //   809 808 80b 73 1c 80c 1a 1b 18 204 104 1d 403 80a db 1f
endmodule

module Registers (
  input  Reg_write,
  input  Clock,
  input  [3:0] Read_register_1,
  input  [3:0] Read_register_2,
  input  [3:0] Writre_register,
  input  [3:0] Write_data,
  input  Clear,
  output [3:0] \output ,
  output [3:0] output_2,
  output [3:0] Read_data_1,
  output [3:0] output_3,
  output [3:0] Read_data_2,
  output [3:0] output_4,
  output [3:0] output_5,
  output [3:0] output_6
);

  wire and_1_out, Demux__7__y7, Demux__11__y4, Demux__12__y3, Demux__13__y2, Demux__14__y1, Demux__15__y0;

  and and_1 (and_1_out, Reg_write, Clock);
  _74238 Demux (
    ._1__A0(Writre_register[0]), ._2__A1(Writre_register[1]), ._3__A2(Writre_register[2]),
    ._4__E1_prime(1'b0), ._5__E2_prime(1'b0), ._6__E3(and_1_out), ._7__Y7(Demux__7__y7),
    ._15__Y0(Demux__15__y0), ._14__Y1(Demux__14__y1), ._13__Y2(Demux__13__y2), ._12__Y3(Demux__12__y3),
    ._11__Y4(Demux__11__y4));  // open: _8__GND, _16__Vcc, _10__Y5, _9__Y6
  Register #(.width(4)) t0 (.D(Write_data), .Q(\output ), .clk(Demux__15__y0), .clr(Clear));  // open: en
  Register #(.width(4)) t1 (.D(Write_data), .Q(output_2), .clk(Demux__14__y1), .clr(Clear));  // open: en
  Register #(.width(4)) t2 (.D(Write_data), .Q(output_3), .clk(Demux__13__y2), .clr(Clear));  // open: en
  Register #(.width(4)) t3 (.D(Write_data), .Q(output_4), .clk(Demux__12__y3), .clr(Clear));  // open: en
  Register #(.width(4)) t4 (.D(Write_data), .Q(output_5), .clk(Demux__11__y4), .clr(Clear));  // open: en
  Register #(.width(4)) sp_111 (.D(Write_data), .Q(output_6), .clk(Demux__7__y7), .clr(Clear));  // open: en
  _4_input_8x1_MUX u_4_input_8x1_mux_1 (
    .t0(\output ), .t1(output_2), .t2(output_3), .t3(output_4), .t4(output_5), .sp(output_6),
    .Register(Read_register_1), .Read_data(Read_data_1));
  _4_input_8x1_MUX u_4_input_8x1_mux_2 (
    .t0(\output ), .t1(output_2), .t2(output_3), .t3(output_4), .t4(output_5), .sp(output_6),
    .Register(Read_register_2), .Read_data(Read_data_2));

  // Notes on the sheet:
  //   5th and 6th bit is zero
endmodule

// 8x1 MUX
module _4_input_8x1_MUX (
  input  [3:0] t0,
  input  [3:0] t1,
  input  [3:0] t2,
  input  [3:0] t3,
  input  [3:0] t4,
  input  [3:0] sp,
  input  [3:0] Register,
  output [3:0] Read_data
);

  _74151 _0 (
    ._1__D3(t3[0]), ._2__D2(t2[0]), ._3__D1(t1[0]), ._4__D0(t0[0]), ._5__Y(Read_data[0]), ._7__nG(1'b0),
    ._15__D4(t4[0]), ._14__D5(1'b0), ._13__D6(1'b0), ._12__D7(sp[0]), ._11__A(Register[0]),
    ._10__B(Register[1]), ._9__C(Register[2]));  // open: _6__W, _8__GND, _16__Vcc
  _74151 _2 (
    ._1__D3(t3[2]), ._2__D2(t2[2]), ._3__D1(t1[2]), ._4__D0(t0[2]), ._5__Y(Read_data[2]), ._7__nG(1'b0),
    ._15__D4(t4[2]), ._14__D5(1'b0), ._13__D6(1'b0), ._12__D7(sp[2]), ._11__A(Register[0]),
    ._10__B(Register[1]), ._9__C(Register[2]));  // open: _6__W, _8__GND, _16__Vcc
  _74151 _1 (
    ._1__D3(t3[1]), ._2__D2(t2[1]), ._3__D1(t1[1]), ._4__D0(t0[1]), ._5__Y(Read_data[1]), ._7__nG(1'b0),
    ._15__D4(t4[1]), ._14__D5(1'b0), ._13__D6(1'b0), ._12__D7(sp[1]), ._11__A(Register[0]),
    ._10__B(Register[1]), ._9__C(Register[2]));  // open: _6__W, _8__GND, _16__Vcc
  _74151 _3 (
    ._1__D3(t3[3]), ._2__D2(t2[3]), ._3__D1(t1[3]), ._4__D0(t0[3]), ._5__Y(Read_data[3]), ._7__nG(1'b0),
    ._15__D4(t4[3]), ._14__D5(1'b0), ._13__D6(1'b0), ._12__D7(sp[3]), ._11__A(Register[0]),
    ._10__B(Register[1]), ._9__C(Register[2]));  // open: _6__W, _8__GND, _16__Vcc

  // Notes on the sheet:
  //   $zero
endmodule

module Main (
  output [3:0] t4,
  output [3:0] t3,
  output [3:0] Result,
  output [3:0] t2,
  output [3:0] t1,
  output [3:0] t0,
  output [3:0] Data,
  output [3:0] out_8,
  output [3:0] out_9,
  output [3:0] out_10,
  output [3:0] out_11,
  output [3:0] out_12,
  output [3:0] out_13,
  output [3:0] out_14
);

  wire alu_1_zero, Clock_out, control_1_alusrc, control_1_branch, control_1_branch_ne, control_1_jump,
       control_1_memread, control_1_memtoreg, control_1_memwrite, control_1_regdst, control_1_regwrite,
       multiplexer_3_out, Reset_out;
  wire [2:0] control_1_aluop;
  wire [3:0] Data_Memory_read_data, multiplexer_6_out;
  wire [7:0] adder_1_out, adder_2_out, bit_extender_1_out, multiplexer_2_out, multiplexer_5_out, pc_1_pc_out;

  Clock Clock (.out(Clock_out));
  Button Reset (.out(Reset_out));
  // Probe on multiplexer_5_out
  // Probe on pc_1_pc_out
  PC pc_1 (.PC_in(multiplexer_5_out), .Clock(Clock_out), .Reset(Reset_out), .PC_out(pc_1_pc_out));
  Instruction Instruction (
    .PC(pc_1_pc_out), .Opcode(out_8), .Instruction_8_11(out_9), .Instruction_4_7(out_10),
    .Instruction_0_3(out_12));
  Adder adder_1 (.a(pc_1_pc_out), .b(8'h1), .out(adder_1_out));  // open: cin, cout
  Control control_1 (
    .opcode(out_8), .RegDST(control_1_regdst), .Jump(control_1_jump), .Branch(control_1_branch),
    .Branch_NE(control_1_branch_ne), .MemRead(control_1_memread), .MemToReg(control_1_memtoreg),
    .MemWrite(control_1_memwrite), .ALUSrc(control_1_alusrc), .RegWrite(control_1_regwrite),
    .ALUOp(control_1_aluop));  // open: out_12
  assign bit_extender_1_out = {{4{1'b0}}, out_12};  // Bit_Extender bit_extender_1
  Multiplexer #(.width(4), .enable("false")) multiplexer_1 (
    .in0(out_10), .in1(out_12), .out(out_14), .sel(control_1_regdst));
  Adder adder_2 (.a(bit_extender_1_out), .b(adder_1_out), .out(adder_2_out));  // open: cin, cout
  Registers registers_1 (
    .Read_register_1(out_9), .Read_register_2(out_10), .Writre_register(out_14),
    .Write_data(multiplexer_6_out), .Reg_write(control_1_regwrite), .Clock(Clock_out), .Clear(Reset_out),
    .\output (t0), .output_2(t1), .Read_data_1(out_11), .output_3(t2), .Read_data_2(Data), .output_4(t3),
    .output_5(t4));  // open: output_6
  Multiplexer #(.width(8), .enable("false")) multiplexer_2 (
    .in0(adder_1_out), .in1(adder_2_out), .out(multiplexer_2_out), .sel(multiplexer_3_out));
  Multiplexer #(.enable("false")) multiplexer_3 (
    .in0(control_1_branch_ne), .in1(control_1_branch), .out(multiplexer_3_out), .sel(alu_1_zero));
  Multiplexer #(.width(4), .enable("false")) multiplexer_4 (
    .in0(Data), .in1(out_12), .out(out_13), .sel(control_1_alusrc));
  Multiplexer #(.width(8), .enable("false")) multiplexer_5 (
    .in0(multiplexer_2_out), .in1({out_9, out_10}), .out(multiplexer_5_out), .sel(control_1_jump));
  ALU alu_1 (.ALU_op(control_1_aluop), .A(out_11), .B(out_13), .Result(Result), .Zero(alu_1_zero));
  Data_Memory Data_Memory (
    .Address(Result), .Write_Data(Data), .Clock(Clock_out), .Reset(Reset_out),
    .Mem_write(control_1_memwrite), .Mem_read(control_1_memread), .Read_Data(Data_Memory_read_data));
  Multiplexer #(.width(4), .enable("false")) multiplexer_6 (
    .in0(Result), .in1(Data_Memory_read_data), .out(multiplexer_6_out), .sel(control_1_memtoreg));

  // Notes on the sheet:
  //   sw: src, o(dst)
  //   lw; dst, o(src)
  //   1,2,3,4
  //   op, address(dst.data), src.data, off
  //   op, address(src.data), dst off
endmodule
